# Fritzing sketch Thermostat (saved by Fritzing 0.9.3b)
breadboards: 1

parts:
  WeMos_D1_Mini1 = WeMos D1 Mini
  IC1 = ILD213T [package=so08]
  HLK-PM1 = HLK-PM01
  F1 = FUSE [package=fuse_5mm]
  DHT1 = DHT22 Humidity and Temperature Sensor

nets (from the schematic view):
  3V3: WeMos_D1_Mini1.3V3, HLK-PM1.+Vo, DHT1.VDD
  N1: WeMos_D1_Mini1.D1, IC1.A2
  N2: WeMos_D1_Mini1.D5, DHT1.DATA
  N3: WeMos_D1_Mini1.D8, IC1.A1
  GND: WeMos_D1_Mini1.G, IC1.C1, IC1.C2, HLK-PM1.-Vo, DHT1.GND
  N4: HLK-PM1.AC, F1.2
